// Digital circuit lab2_part2.dig as structural Verilog
module lab2_part2 (
  input  in0,
  input  in1,
  input  in2,
  input  in3,
  output seg_a,
  output seg_f,
  output seg_b,
  output seg_g,
  output seg_e,
  output seg_c,
  output seg_d,
  output seg_dp,
  output sign_a,
  output sign_f,
  output sign_b,
  output sign_g,
  output sign_e,
  output sign_c,
  output sign_d,
  output sign_dp
);

  Multiplexer multiplexer_1 (.sel(in3), .in_0(1'b0), .in_1(1'b1), .out(sign_g));
  Seven_Seg seven_seg_1 (.a(1'b0), .b(1'b0), .c(1'b0), .d(1'b0), .e(1'b0), .f(1'b0), .g(sign_g), .dp(1'b0));
  Multiplexer #(.Bits(7), .Selector_Bits(4)) multiplexer_2 (
    .sel({in3, in2, in1, in0}), .in_0(7'b1111110), .in_1(7'b0110000), .in_2(7'b1101101), .in_3(7'b1111001),
    .in_4(7'b0110011), .in_5(7'b1011011), .in_6(7'b1011111), .in_7(7'b1110000), .in_8({7{1'b1}}),
    .in_9(7'b1110000), .in_10(7'b1011111), .in_11(7'b1011011), .in_12(7'b0110011), .in_13(7'b1111001),
    .in_14(7'b1101101), .in_15(7'b0110000), .out({seg_a, seg_b, seg_c, seg_d, seg_e, seg_f, seg_g}));
  Seven_Seg seven_seg_2 (.a(seg_a), .b(seg_b), .c(seg_c), .d(seg_d), .e(seg_e), .f(seg_f), .g(seg_g), .dp(1'b0));

  assign seg_dp = 1'b0;
  assign sign_a = 1'b0;
  assign sign_b = 1'b0;
  assign sign_c = 1'b0;
  assign sign_d = 1'b0;
  assign sign_dp = 1'b0;
  assign sign_e = 1'b0;
  assign sign_f = 1'b0;

  // Notes on the sheet:
  //   Interface (do not edit the content inside this box)
  //   Outputs:
  //   Inputs
  //   Sign
  //   Decimal Number
endmodule

/* Test case:
in3 in2 in1 in0  sign_a sign_b sign_c sign_d sign_e sign_f sign_g  seg_a seg_b seg_c seg_d seg_e seg_f seg_g
 0   0   0   0    0      0      0      0      0      0      0       1     1     1     1     1     1     0
*/
