// Digital circuit part_b.dig as structural Verilog
module part_b (
  input  in_0,
  input  in_1,
  input  in_2,
  output out_0
);

  nand nand_1 (out_0, in_0, in_1, in_2);
endmodule

/* Test case part_b_test:
in_0 in_1 in_2 out_0
 0    0    0      1   
 0    0    1      1
 0    1    0      1
 0    1    1      1
 1    0    0      1
 1    0    1      1
 1    1    0      1
 1    1    1      0
*/
